// Digital circuit calculator.dig as structural Verilog
module calculator (
);

  wire _0, _1, _2, _3, _4, _5, _6, _7, _8, _9, and_1_out, and_2_out, bol, calstr, carp, cikar, clr, en_num1,
       en_num2, eq, err, key, led, led__plus, led_t, ledx, say2, sign, topla, xor_1_out, xor_2_out;
  wire [3:0] iss, op1_bcd0, op1_bcd1, op1_bcd2, op1_bcd3, op2_bcd0, op2_bcd1, op2_bcd2, op2_bcd3, res0, res1,
       res2, res3;
  wire [6:0] op1_d0, op1_d1, op1_d2, op1_d3, op2_d0, op2_d1, op2_d2, op2_d3, res_d0, res_d1, res_d2, res_d3,
       sign_disp;

  Button u__0 (.out(_0));
  Button u__1 (.out(_1));
  Button u__2 (.out(_2));
  Button u__3 (.out(_3));
  Button u__4 (.out(_4));
  Button u__5 (.out(_5));
  Button u__6 (.out(_6));
  Button u__7 (.out(_7));
  Button u__8 (.out(_8));
  Button u__9 (.out(_9));
  Button u_eq (.out(eq));
  Button c (.out(clr));
  LED led_1 (.in(clr));
  Button plus (.out(iss[0]));
  Button button (.out(iss[1]));
  Button button_2 (.out(iss[2]));
  Button x (.out(iss[3]));
  Seven_Seg seven_seg_1 (
    .a(sign_disp[6]), .b(sign_disp[5]), .c(sign_disp[4]), .d(sign_disp[3]), .e(sign_disp[2]),
    .f(sign_disp[1]), .g(sign_disp[0]), .dp(1'b0));
  Seven_Seg seven_seg_2 (
    .a(op1_d3[6]), .b(op1_d3[5]), .c(op1_d3[4]), .d(op1_d3[3]), .e(op1_d3[2]), .f(op1_d3[1]), .g(op1_d3[0]),
    .dp(1'b0));
  Seven_Seg seven_seg_3 (
    .a(op2_d3[6]), .b(op2_d3[5]), .c(op2_d3[4]), .d(op2_d3[3]), .e(op2_d3[2]), .f(op2_d3[1]), .g(op2_d3[0]),
    .dp(1'b0));
  Seven_Seg seven_seg_4 (
    .a(res_d3[6]), .b(res_d3[5]), .c(res_d3[4]), .d(res_d3[3]), .e(res_d3[2]), .f(res_d3[1]), .g(res_d3[0]),
    .dp(1'b0));
  LED plus_2 (.in(led__plus));
  Seven_Seg seven_seg_5 (
    .a(op1_d2[6]), .b(op1_d2[5]), .c(op1_d2[4]), .d(op1_d2[3]), .e(op1_d2[2]), .f(op1_d2[1]), .g(op1_d2[0]),
    .dp(1'b0));
  Seven_Seg seven_seg_6 (
    .a(op2_d2[6]), .b(op2_d2[5]), .c(op2_d2[4]), .d(op2_d2[3]), .e(op2_d2[2]), .f(op2_d2[1]), .g(op2_d2[0]),
    .dp(1'b0));
  Seven_Seg seven_seg_7 (
    .a(res_d2[6]), .b(res_d2[5]), .c(res_d2[4]), .d(res_d2[3]), .e(res_d2[2]), .f(res_d2[1]), .g(res_d2[0]),
    .dp(1'b0));
  LED led_2 (.in(led));
  Seven_Seg seven_seg_8 (
    .a(op1_d1[6]), .b(op1_d1[5]), .c(op1_d1[4]), .d(op1_d1[3]), .e(op1_d1[2]), .f(op1_d1[1]), .g(op1_d1[0]),
    .dp(1'b0));
  LED led_3 (.in(led_t));
  Seven_Seg seven_seg_9 (
    .a(op2_d1[6]), .b(op2_d1[5]), .c(op2_d1[4]), .d(op2_d1[3]), .e(op2_d1[2]), .f(op2_d1[1]), .g(op2_d1[0]),
    .dp(1'b0));
  Seven_Seg seven_seg_10 (
    .a(res_d1[6]), .b(res_d1[5]), .c(res_d1[4]), .d(res_d1[3]), .e(res_d1[2]), .f(res_d1[1]), .g(res_d1[0]),
    .dp(1'b0));
  Seven_Seg seven_seg_11 (
    .a(op1_d0[6]), .b(op1_d0[5]), .c(op1_d0[4]), .d(op1_d0[3]), .e(op1_d0[2]), .f(op1_d0[1]), .g(op1_d0[0]),
    .dp(1'b0));
  LED x_2 (.in(ledx));
  Seven_Seg seven_seg_12 (
    .a(op2_d0[6]), .b(op2_d0[5]), .c(op2_d0[4]), .d(op2_d0[3]), .e(op2_d0[2]), .f(op2_d0[1]), .g(op2_d0[0]),
    .dp(1'b0));
  Seven_Seg seven_seg_13 (
    .a(res_d0[6]), .b(res_d0[5]), .c(res_d0[4]), .d(res_d0[3]), .e(res_d0[2]), .f(res_d0[1]), .g(res_d0[0]),
    .dp(1'b0));
  and and_1 (and_1_out, en_num1, key);
  and and_2 (and_2_out, en_num2, key);
  display3 #(.applicationType("IVERILOG")) u_display3 (
    .clear(clr), .sign(sign), .en_res(calstr), .error(err), .res0(res0), .res1(res1), .res2(res2),
    .res3(res3), .display0(res_d0), .display1(res_d1), .display2(res_d2), .display3(res_d3),
    .sign_disp(sign_disp));
  turnike #(.applicationType("IVERILOG")) u_turnike (
    .say2(say2), .calculate(eq), .clear(clr), .hangislem(iss), .en_num1(en_num1), .en_num2(en_num2),
    .disp_topla(led__plus), .disp_cikar(led), .disp_bol(led_t), .disp_carp(ledx), .topla(topla),
    .cikar(cikar), .bol(bol), .carp(carp));
  display1 #(.applicationType("IVERILOG")) u_display1 (
    .key(and_1_out), .clear(clr), .pressed({_9, _8, _7, _6, _5, _4, _3, _2, _1, _0}), .out0(op1_bcd0),
    .out1(op1_bcd1), .out2(op1_bcd2), .out3(op1_bcd3), .display0(op1_d0), .display1(op1_d1),
    .display2(op1_d2), .display3(op1_d3));
  display2 #(.applicationType("IVERILOG")) u_display2 (
    .key(and_2_out), .clear(clr), .pressed({_9, _8, _7, _6, _5, _4, _3, _2, _1, _0}), .out0(op2_bcd0),
    .out1(op2_bcd1), .out2(op2_bcd2), .out3(op2_bcd3), .display0(op2_d0), .display1(op2_d1),
    .display2(op2_d2), .display3(op2_d3));
  calculator #(.applicationType("IVERILOG")) u_calculator (
    .topla(topla), .cikar(cikar), .bol(bol), .carp(carp), .clear(clr), .s1_d0(op1_bcd0), .s1_d1(op1_bcd1),
    .s1_d2(op1_bcd2), .s1_d3(op1_bcd3), .s2_d0(op2_bcd0), .s2_d1(op2_bcd1), .s2_d2(op2_bcd2),
    .s2_d3(op2_bcd3), .res0(res0), .res1(res1), .res2(res2), .res3(res3), .error(err), .sign(sign),
    .disp(calstr));
  xor xor_1 (xor_1_out, _0, _1, _2, _3, _4);
  xor xor_2 (xor_2_out, _5, _6, _7, _8, _9);
  xor xor_3 (say2, iss[0], iss[1], iss[2], iss[3]);
  xor xor_4 (key, xor_1_out, xor_2_out);

  // Other names for the same wires on the sheet: press[9:0] = {_9, _8, _7, _6, _5, _4, _3, _2, _1, _0}; plus = iss[0];
  //   tunnel = iss[1]; tunnel_t = iss[2]; x = iss[3]
endmodule

/* Code of display3:
module display3(
    input clear,
    input sign,
    input en_res,
    input error,
    input [3:0] res0,
    input [3:0] res1,
    input [3:0] res2,
    input [3:0] res3,
    output reg [6:0] display0,
    output reg [6:0] display1,
    output reg [6:0] display2,
    output reg [6:0] display3,
    output reg [6:0] sign_disp
);

always @(posedge en_res or posedge clear or posedge error) begin
    if (clear) begin
        display0 <= 7'b0000000;
        display1 <= 7'b0000000;
        display2 <= 7'b0000000;
        display3 <= 7'b0000000;
        sign_disp <= 7'b0000000;
    end 
else if ( error) begin 
        display0 <= 7'b0000101;
        display1 <= 7'b0011101;
        display2 <= 7'b0000101;
        display3 <= 7'b0000101;
        sign_disp <=7'b1001111;
end
else if (!error) begin
        case(res0)
            4'b0000: display0 = 7'b1111110; //0
            4'b0001: display0 = 7'b0110000; //1
            4'b0010: display0 = 7'b1101101; //2
            4'b0011: display0 = 7'b1111001; //3
            4'b0100: display0 = 7'b0110011; //4
            4'b0101: display0 = 7'b1011011; //5
            4'b0110: display0 = 7'b1011111; //6
            4'b0111: display0 = 7'b1110000; //7
            4'b1000: display0 = 7'b1111111; //8
            4'b1001: display0 = 7'b1111011; //9
            default: display0 = 7'b0000000;
        endcase

        case(res1)
            4'b0000: display1 = 7'b1111110; //0
            4'b0001: display1 = 7'b0110000; //1
            4'b0010: display1 = 7'b1101101; //2
            4'b0011: display1 = 7'b1111001; //3
            4'b0100: display1 = 7'b0110011; //4
            4'b0101: display1 = 7'b1011011; //5
            4'b0110: display1 = 7'b1011111; //6
            4'b0111: display1 = 7'b1110000; //7
            4'b1000: display1 = 7'b1111111; //8
            4'b1001: display1 = 7'b1111011; //9
            default: display1 = 7'b0000000;
        endcase

        case(res2)
            4'b0000: display2 = 7'b1111110; //0
            4'b0001: display2 = 7'b0110000; //1
            4'b0010: display2 = 7'b1101101; //2
            4'b0011: display2 = 7'b1111001; //3
            4'b0100: display2 = 7'b0110011; //4
            4'b0101: display2 = 7'b1011011; //5
            4'b0110: display2 = 7'b1011111; //6
            4'b0111: display2 = 7'b1110000; //7
            4'b1000: display2 = 7'b1111111; //8
            4'b1001: display2 = 7'b1111011; //9
            default: display2 = 7'b0000000;
        endcase

        case(res3)
            4'b0000: display3 = 7'b1111110; //0
            4'b0001: display3 = 7'b0110000; //1
            4'b0010: display3 = 7'b1101101; //2
            4'b0011: display3 = 7'b1111001; //3
            4'b0100: display3 = 7'b0110011; //4
            4'b0101: display3 = 7'b1011011; //5
            4'b0110: display3 = 7'b1011111; //6
            4'b0111: display3 = 7'b1110000; //7
            4'b1000: display3 = 7'b1111111; //8
            4'b1001: display3 = 7'b1111011; //9
            default: display3 = 7'b0000000;
        endcase

        if (!error && !sign)
            sign_disp = 7'b0000000;
        else
            sign_disp = 7'b0000001;
    end
end

endmodule
*/

/* Code of turnike:
module turnike(
  input say2,
  input calculate,
  input clear,
  input [3:0] hangislem,
  output reg en_num1,
  output reg en_num2,
  output reg disp_topla,
  output reg disp_cikar,
  output reg disp_bol,
  output reg disp_carp,
  output reg topla,
  output reg cikar,
  output reg bol,
  output reg carp
);

always @(posedge clear or posedge calculate or posedge say2) begin
  if (clear) begin
    en_num1 <= 1;
    en_num2 <= 0;
disp_topla<= 0;
disp_cikar<= 0;
disp_bol<= 0;
disp_carp<= 0;

topla <=0;
cikar <=0;
bol<= 0;
carp<= 0;


  end
  else if (say2) begin
    en_num1 <= 0;
    en_num2 <= 1;
case (hangislem)
    4'b0001: begin
      disp_topla = 1;
      disp_cikar = 0;
      disp_bol = 0;
      disp_carp = 0;

    end 

    4'b0010: begin
      disp_topla = 0;
      disp_cikar = 1;
      disp_bol = 0;
      disp_carp = 0;
    end 

    4'b0100: begin
      disp_topla = 0;
      disp_cikar = 0;
      disp_bol = 1;
      disp_carp = 0;
    end 

    4'b1000: begin
      disp_topla = 0;
      disp_cikar = 0;
      disp_bol = 0;
      disp_carp = 1;
    end 

    default: begin
      disp_topla = 0;
      disp_cikar = 0;
      disp_bol = 0;
      disp_carp = 0;
    end 
  endcase
  end
  else if (calculate && ! en_num1) begin
    en_num1 <= 0;
    en_num2 <= 0;
      topla <= disp_topla ;
      cikar <= disp_cikar;
      bol <= disp_bol ;
      carp <= disp_carp ;
   
  end
end

endmodule
*/

/* Code of display1:
module display1(
    input key,
    input clear,
    input [9:0] pressed,
    output reg [3:0] out0,
    output reg [3:0] out1,
    output reg [3:0] out2,
    output reg [3:0] out3,
    output reg [6:0] display0,
    output reg [6:0] display1,
    output reg [6:0] display2,
    output reg [6:0] display3
);

always @( posedge key or posedge clear) begin
    if (clear) begin
        
        out0 <= 4'b0000;
        out1 <= 4'b0000;
        out2 <= 4'b0000;
        out3 <= 4'b0000;
        display0 <= 7'b0000000;
        display1 <= 7'b0000000;
        display2 <= 7'b0000000;
        display3 <= 7'b0000000;
    end else if ( out3 == 4'b0000)begin
       
        out3 <= out2;
        out2 <= out1;
        out1 <= out0;
        display3 <= display2;
        display2 <= display1;
        display1 <= display0;

       
        case (pressed)
            10'b0000000001: begin
                display0 = 7'b1111110; //0 
                out0 = 4'b0000;
            end
            10'b0000000010: begin
                display0 = 7'b0110000; //1
                out0 = 4'b0001;
            end
            10'b0000000100: begin
                display0 = 7'b1101101; //2
                out0 = 4'b0010;
            end
            10'b0000001000: begin
                display0 = 7'b1111001; //3
                out0 = 4'b0011;
            end
            10'b0000010000: begin
                display0 = 7'b0110011; //4
                out0 = 4'b0100;
            end
            10'b0000100000: begin 
                display0 = 7'b1011011; //5
                out0 = 4'b0101;
            end
            10'b0001000000: begin
                display0 = 7'b1011111; //6
                out0 = 4'b0110;
            end
            10'b0010000000: begin
                display0 = 7'b1110000; //7 
                out0 = 4'b0111;
            end
            10'b0100000000: begin
                display0 = 7'b1111111; //8  
                out0 = 4'b1000;
            end 
            10'b1000000000: begin
                display0 = 7'b1111011; //9 
                out0 = 4'b1001;
            end 
            default: begin
                // Default durumu
                display0 = 7'b0000000;
                out0 = 4'b0000;
            end 
        endcase
    end
end

endmodule
*/

/* Code of display2:
module display2(
    input key,
    input clear,
    input [9:0] pressed,
    output reg [3:0] out0,
    output reg [3:0] out1,
    output reg [3:0] out2,
    output reg [3:0] out3,
    output reg [6:0] display0,
    output reg [6:0] display1,
    output reg [6:0] display2,
    output reg [6:0] display3
);

always @(posedge key or posedge clear) begin
    if (clear) begin
        // Clear işlemi
        out0 <= 4'b0000;
        out1 <= 4'b0000;
        out2 <= 4'b0000;
        out3 <= 4'b0000;
        display0 <= 7'b0000000;
        display1 <= 7'b0000000;
        display2 <= 7'b0000000;
        display3 <= 7'b0000000;
    end else if ( out3 == 4'b0000) begin
     
        out3 <= out2;
        out2 <= out1;
        out1 <= out0;
        display3 <= display2;
        display2 <= display1;
        display1 <= display0;

     
        case (pressed)
            10'b0000000001: begin
                display0 = 7'b1111110; //0 
                out0 = 4'b0000;
            end
            10'b0000000010: begin
                display0 = 7'b0110000; //1
                out0 = 4'b0001;
            end
            10'b0000000100: begin
                display0 = 7'b1101101; //2
                out0 = 4'b0010;
            end
            10'b0000001000: begin
                display0 = 7'b1111001; //3
                out0 = 4'b0011;
            end
            10'b0000010000: begin
                display0 = 7'b0110011; //4
                out0 = 4'b0100;
            end
            10'b0000100000: begin 
                display0 = 7'b1011011; //5
                out0 = 4'b0101;
            end
            10'b0001000000: begin
                display0 = 7'b1011111; //6
                out0 = 4'b0110;
            end
            10'b0010000000: begin
                display0 = 7'b1110000; //7 
                out0 = 4'b0111;
            end
            10'b0100000000: begin
                display0 = 7'b1111111; //8  
                out0 = 4'b1000;
            end 
            10'b1000000000: begin
                display0 = 7'b1111011; //9 
                out0 = 4'b1001;
            end 
            default: begin
                // Default durumu
                display0 = 7'b0000000;
                out0 = 4'b0000;
            end 
        endcase
    end
end

endmodule
*/

/* Code of calculator:
module calculator(
    input topla,
    input cikar,
    input bol,
    input carp,

    input clear,
    input [3:0] s1_d0,
    input [3:0] s1_d1,
    input [3:0] s1_d2,
    input [3:0] s1_d3,
    input [3:0] s2_d0,
    input [3:0] s2_d1,
    input [3:0] s2_d2,
    input [3:0] s2_d3,
    output reg [3:0] res0,
    output reg [3:0] res1,
    output reg [3:0] res2,
    output reg [3:0] res3,
    output reg error,
    output reg sign,
    output reg disp
);

    reg [3:0] carry;
    reg [13:0] op1; 
    reg [13:0] op2;
    reg [13:0] resondort;
    reg borrow;

    always @ (posedge cikar or posedge bol or posedge carp or posedge topla or posedge clear) begin
        if (clear) begin
            res0 <= 4'b0;
            res1 <= 4'b0;
            res2 <= 4'b0;
            res3 <= 4'b0;
            error <= 0;
            carry <= 4'b0;
            sign <= 0;
            disp <= 0;
            op1 <= 14'b0;
            op2 <= 14'b0;
            resondort <= 14'b0;
        end
        else begin
            if (topla) begin
                carry[0] = (s1_d0 + s2_d0) > 9 ? 1 : 0;
                carry[1] = (s1_d1 + s2_d1 + carry[0]) > 9 ? 1 : 0;
                carry[2] = (s1_d2 + s2_d2 + carry[1]) > 9 ? 1 : 0;
                carry[3] = (s1_d3 + s2_d3 + carry[2]) > 9 ? 1 : 0;

                res0 = (s1_d0 + s2_d0) % 10;
                res1 = (s1_d1 + s2_d1 + carry[0]) % 10;
                res2 = (s1_d2 + s2_d2 + carry[1]) % 10;
                res3 = (s1_d3 + s2_d3 + carry[2]) % 10;
                disp = 1;

                error = carry[3];
            end
        else if (cikar) begin
op1 = s1_d0 + s1_d1 * 10 + s1_d2 * 100 + s1_d3 * 1000;
op2 = s2_d0 + s2_d1 * 10 + s2_d2 * 100 + s2_d3 * 1000;
         if (op1 >= op2) begin
                resondort = op1 - op2;
                res0 = resondort % 10;
                res1 = (resondort % 100) / 10;
                res2 = (resondort % 1000) / 100;
                res3 = (resondort % 10000) / 1000;
                sign = 0;
            end else begin
                resondort = op2 - op1;
                res0 = resondort % 10;
                res1 = (resondort % 100) / 10;
                res2 = (resondort % 1000) / 100;
                res3 = (resondort % 10000) / 1000;
                sign = 1;
            end
disp = 1;
            end else if (carp) begin
            op1 = s1_d0 + s1_d1 * 10 + s1_d2 * 100 + s1_d3 * 1000;
            op2 = s2_d0 + s2_d1 * 10 + s2_d2 * 100 + s2_d3 * 1000;

            resondort = op1 * op2;

            res0 = resondort % 10;
            res1 = (resondort % 100) / 10;
            res2 = (resondort % 1000) / 100;
            res3 = (resondort % 10000) / 1000;

            op1 = resondort % 10000;

            if (op1 >= 0) begin
                error = 0;
                disp = 1;
            end else begin
                error = 1;
                disp = 0;
            end 
          end else if (bol) begin
            op1 = s1_d0 + s1_d1 * 10 + s1_d2 * 100 + s1_d3 * 1000;
            op2 = s2_d0 + s2_d1 * 10 + s2_d2 * 100 + s2_d3 * 1000;

            if (op2 == 0) begin
                // Bölme sıfıra bölünemez
                error = 1;
                disp = 0;
            end else begin
                resondort = op1 / op2;
               
                res0 = resondort % 10;
                res1 = (resondort % 100) / 10;
                res2 = (resondort % 1000) / 100;
                res3 = (resondort % 10000) / 1000;

                error = 0;
                disp = 1;
            end
          end
        end
    end
endmodule
*/
